// Logisim project 5-Stage-Pipeline-MAIN.circ as structural Verilog: 1 circuit, main circuit main
module main (
);

  wire and_1_out, button_1_out, clock_1_out, decoder_1_1_p3, Instruction_Splitter_p1,
       Instruction_Splitter_p3, Instruction_Splitter_p4, Instruction_Splitter_p5, Instruction_Splitter_p6,
       Instruction_Splitter_p7, Instruction_Splitter_p8, Instruction_Splitter_p9, not_1_out, Registers_p3,
       Registers_p7, undriven_2, undriven_4, undriven_5;
  wire [7:0] adder_1_out, multiplexer_2_out, multiplexer_3_out, PC_q, undriven, undriven_3;
  wire [15:0] ID_EX_2_q, ID_EX_q, IF_ID_q, multiplexer_5_out, Registers_p5, Registers_p6, rom_1_data,
       Sign_Extender_p6, Sign_Extender_p7, Sign_Extender_p8;

  Multiplexer multiplexer_1 ();  // open: in0, in1, out, sel, en
  Clock clock_1 (.out(clock_1_out));
  Multiplexer #(.width(8), .enable("false")) multiplexer_2 (
    .in0(adder_1_out), .in1(undriven), .out(multiplexer_2_out), .sel(undriven_2));
  Multiplexer #(.width(8), .enable("false")) multiplexer_3 (
    .in0(multiplexer_2_out), .in1(undriven_3), .out(multiplexer_3_out), .sel(undriven_4));
  not not_1 (not_1_out, undriven_5);
  Register PC (.D(multiplexer_3_out), .en(and_1_out), .Q(PC_q), .clk(clock_1_out), .clr(button_1_out));
  Button button_1 (.out(button_1_out));
  and and_1 (and_1_out, not_1_out, 1'b1);
  Adder adder_1 (.a(PC_q), .b(8'h1), .out(adder_1_out));  // open: cin, cout
  ROM #(.dataWidth(16)) rom_1 (.addr(PC_q), .data(rom_1_data), .sel(1'b1));
  Register #(.width(16)) IF_ID (.D(rom_1_data), .Q(IF_ID_q), .clk(clock_1_out));  // open: en, clr
  // InstructionSplitter Instruction_Splitter: pin names not known; wires that end beside it: Instruction_Splitter_p1, IF_ID_q, Instruction_Splitter_p3, Instruction_Splitter_p4, Instruction_Splitter_p5, Instruction_Splitter_p6, Instruction_Splitter_p7, Instruction_Splitter_p8, Instruction_Splitter_p9, Instruction_Splitter_p6
  // Decoder_1 decoder_1_1: pin names not known; wires that end beside it: Instruction_Splitter_p3, Instruction_Splitter_p7, decoder_1_1_p3
  // Decoder_2_ALU decoder_2_alu_1: pin names not known
  // RegisterFile Registers: pin names not known; wires that end beside it: Instruction_Splitter_p4, Instruction_Splitter_p5, Registers_p3, clock_1_out, Registers_p5, Registers_p6, Registers_p7
  // SignExtend Sign_Extender: pin names not known; wires that end beside it: decoder_1_1_p3, Registers_p3, Instruction_Splitter_p8, Instruction_Splitter_p9, Registers_p7, Sign_Extender_p6, Sign_Extender_p7, Sign_Extender_p8
  Register #(.width(16)) ID_EX (.D(Registers_p5), .Q(ID_EX_q), .clk(clock_1_out));  // open: en, clr
  Register #(.width(16)) ID_EX_2 (.D(Registers_p6), .Q(ID_EX_2_q), .clk(clock_1_out));  // open: en, clr
  Register #(.width(16)) ID_EX_3 ();  // open: D, en, Q, clk, clr
  Register #(.width(16)) ID_EX_4 ();  // open: D, en, Q, clk, clr
  Multiplexer #(.select(2), .width(16), .enable("false")) multiplexer_4 (
    .in1(ID_EX_q), .in2(Sign_Extender_p7), .in3(Sign_Extender_p8));  // open: in0, out, sel
  Multiplexer #(.select(2), .width(16), .enable("false")) multiplexer_5 (
    .in1(ID_EX_2_q), .in2(Sign_Extender_p7), .in3(Sign_Extender_p8), .out(multiplexer_5_out));  // open: in0, sel
  // sixteen_bit_ALU ALU_NEEDING_CHANGED: pin names not known; wires that end beside it: clock_1_out
  Multiplexer #(.width(16), .enable("false")) multiplexer_6 (
    .in0(multiplexer_5_out), .in1(Sign_Extender_p6));  // open: out, sel
  Register #(.width(16)) EX_MEM ();  // open: D, en, Q, clk, clr
  Register #(.width(16)) MEM_WB ();  // open: D, en, Q, clk, clr
  RAM #(.dataWidth(16)) ram_1 ();  // open: addr, data, sel, clk, ld, clr
  Multiplexer multiplexer_7 ();  // open: in0, in1, out, sel, en

  // Notes on the sheet:
  //   Imm
  //   Branch Address
  //   ImmToPC
  //   RegToPC
  //   Halt Decoder
  //   IF
  //   ID
  //   WriteBack
  //   Imm Gen
  //   EX
  //   MEM
  //   WB
endmodule
