// Logisim project 5-Stage-Pipeline-MAIN_TEST.circ as structural Verilog: 1 circuit, main circuit main
module main (
);

  wire _1CycleWait_q, and_1_out, and_2_out, clock_1_out, comparator_1_eq, decoder_1_1_alusrc,
       decoder_1_1_branch, decoder_1_1_halt, decoder_1_1_immsrc, decoder_1_1_memread, decoder_1_1_memtoreg,
       decoder_1_1_memwrite, decoder_1_1_put, decoder_1_1_regdst, decoder_1_1_regwrite,
       EX_MEM_Control_halt_2, EX_MEM_Control_memread_2, EX_MEM_Control_memtoreg_2, EX_MEM_Control_memwrite_2,
       EX_MEM_Control_regwrite_2, hazard_detection_1_stall, ID_EX_Control_alusrc_2, ID_EX_Control_halt_2,
       ID_EX_Control_immsrc_2, ID_EX_Control_memread_2, ID_EX_Control_memtoreg_2, ID_EX_Control_memwrite_2,
       ID_EX_Control_put_2, ID_EX_Control_regdst_2, ID_EX_Control_regwrite_2, Instruction_Splitter_p6,
       Instruction_Splitter_p7, Instruction_Splitter_p8, MEM_WB_Control_halt_2, MEM_WB_Control_memtoreg_2,
       not_1_out, not_2_out, not_3_out, not_4_out, Registers_p5, RESET_out;
  wire [1:0] Forwawrding_Unit_forward_a, Forwawrding_Unit_forward_b;
  wire [2:0] EX_MEM_Main_Latch_write_register_2, ID_EX_Main_Latch_write_register_2, Instruction_Splitter_p3,
       Instruction_Splitter_p4, Instruction_Splitter_p5, register_1_q, register_2_q, Registers_p3;
  wire [3:0] ALU_Control_aluop, ID_EX_Main_Latch_alu_control_2, Instruction_Splitter_p2;
  wire [7:0] adder_1_out, adder_2_out, IF_ID_PC_q, Instruction_Splitter_p9, multiplexer_2_out, PC_q, undriven;
  wire [15:0] EX_MEM_Main_Latch_alu_result_2, EX_MEM_Main_Latch_read_data_2_2, ID_EX_Main_Latch_imm_gen_2,
       ID_EX_Main_Latch_read_data_1_2, ID_EX_Main_Latch_read_data_2_2, IF_ID_q, MRM_WB_Main_Latch_address_2,
       MRM_WB_Main_Latch_read_data_2, multiplexer_3_out, multiplexer_4_out, multiplexer_5_out, ram_1_data,
       register_3_q, Registers_p4, Registers_p7, Registers_p8, rom_1_data, Sign_Extender__Imm_Gen_p3,
       sixteen_bit_alu_1_p4;

  Multiplexer multiplexer_1 ();  // open: in0, in1, out, sel, en
  Clock clock_1 (.out(clock_1_out));
  Multiplexer #(.width(8), .enable("false")) multiplexer_2 (
    .in0(adder_1_out), .in1(adder_2_out), .out(multiplexer_2_out), .sel(and_2_out));
  not not_1 (not_1_out, hazard_detection_1_stall);
  Register PC (.D(multiplexer_2_out), .en(and_1_out), .Q(PC_q), .clk(clock_1_out), .clr(RESET_out));
  and and_1 (and_1_out, not_1_out, not_2_out, 1'b1);
  not not_2 (not_2_out, ID_EX_Control_halt_2);
  Button RESET (.out(RESET_out));
  Adder adder_1 (.a(PC_q), .b(8'h1), .out(adder_1_out));  // open: cin, cout
  ROM #(.dataWidth(16)) rom_1 (.addr(PC_q), .data(rom_1_data), .sel(1'b1));
  not not_3 (not_3_out, hazard_detection_1_stall);
  Register #(.width(16)) IF_ID (.D(rom_1_data), .en(not_3_out), .Q(IF_ID_q), .clk(clock_1_out), .clr(RESET_out));
  Register IF_ID_PC (.D(PC_q), .en(not_3_out), .Q(IF_ID_PC_q), .clk(clock_1_out), .clr(RESET_out));
  // InstructionSplitter Instruction_Splitter: pin names not known; wires that end beside it: IF_ID_q, Instruction_Splitter_p2, Instruction_Splitter_p3, Instruction_Splitter_p4, Instruction_Splitter_p5, Instruction_Splitter_p6, Instruction_Splitter_p7, Instruction_Splitter_p8, Instruction_Splitter_p9, Instruction_Splitter_p6
  not not_4 (not_4_out, hazard_detection_1_stall);
  Decoder_2_ALU ALU_Control (
    .Opcode3(Instruction_Splitter_p2[3]), .Opcode2(Instruction_Splitter_p2[2]),
    .Opcode1(Instruction_Splitter_p2[1]), .Opcode0(Instruction_Splitter_p2[0]),
    .Subop(Instruction_Splitter_p7), .Enable(not_4_out), .ALUOP(ALU_Control_aluop));
  Decoder_1 decoder_1_1 (
    .Opcode3(Instruction_Splitter_p2[3]), .Opcode2(Instruction_Splitter_p2[2]),
    .Opcode1(Instruction_Splitter_p2[1]), .Opcode0(Instruction_Splitter_p2[0]),
    .Subop(Instruction_Splitter_p7), .Unisigned(Instruction_Splitter_p8), .Enable(not_4_out),
    .RegWrite(decoder_1_1_regwrite), .RegDst(decoder_1_1_regdst), .ALUSrc(decoder_1_1_alusrc),
    .MemRead(decoder_1_1_memread), .MemWrite(decoder_1_1_memwrite), .MemToReg(decoder_1_1_memtoreg),
    .Branch(decoder_1_1_branch), .Halt(decoder_1_1_halt), .Put(decoder_1_1_put), .ImmSrc(decoder_1_1_immsrc));
  // RegisterFile Registers: pin names not known; wires that end beside it: Instruction_Splitter_p3, Instruction_Splitter_p4, Registers_p3, Registers_p4, Registers_p5, clock_1_out, Registers_p7, Registers_p8
  and and_2 (and_2_out, comparator_1_eq, decoder_1_1_branch);
  // SignExtend Sign_Extender__Imm_Gen: pin names not known; wires that end beside it: Instruction_Splitter_p8, Instruction_Splitter_p9, Sign_Extender__Imm_Gen_p3
  Comparator #(.width(16)) comparator_1 (.a(Registers_p7), .b(Registers_p8), .eq(comparator_1_eq));  // open: gt, lt
  Adder adder_2 (.a(Instruction_Splitter_p9), .b(IF_ID_PC_q), .out(adder_2_out));  // open: cin, cout
  Register #(.width(3)) register_1 (
    .D(Instruction_Splitter_p3), .Q(register_1_q), .clk(clock_1_out), .clr(RESET_out));  // open: en
  Register #(.width(3)) register_2 (
    .D(Instruction_Splitter_p4), .Q(register_2_q), .clk(clock_1_out), .clr(RESET_out));  // open: en
  Control_Latch ID_EX_Control (
    .RegWrite(decoder_1_1_regwrite), .RegDst(decoder_1_1_regdst), .ALUSrc(decoder_1_1_alusrc),
    .MemRead(decoder_1_1_memread), .MemWrite(decoder_1_1_memwrite), .MemToReg(decoder_1_1_memtoreg),
    .Halt(decoder_1_1_halt), .Put(decoder_1_1_put), .ImmSrc(decoder_1_1_immsrc),
    .RegWrite_2(ID_EX_Control_regwrite_2), .RegDst_2(ID_EX_Control_regdst_2),
    .ALUSrc_2(ID_EX_Control_alusrc_2), .MemRead_2(ID_EX_Control_memread_2),
    .MemWrite_2(ID_EX_Control_memwrite_2), .MemToReg_2(ID_EX_Control_memtoreg_2),
    .Halt_2(ID_EX_Control_halt_2), .Put_2(ID_EX_Control_put_2), .ImmSrc_2(ID_EX_Control_immsrc_2),
    .Clock(clock_1_out));  // open: Branch, Branch_2, Enable
  Hazard_Detection hazard_detection_1 (.Stall(hazard_detection_1_stall));  // open: ID_EX_MemRead, ID_EX_RegisterRead, IF_ID_RegisterR1, IF_ID_RegisterR2
  ID_EX_Main_Latch ID_EX_Main_Latch (
    .Read_Data_1(Registers_p7), .Read_Data_2(Registers_p8), .Imm_Gen(Sign_Extender__Imm_Gen_p3),
    .ALU_Control(ALU_Control_aluop), .Read_Data_1_2(ID_EX_Main_Latch_read_data_1_2),
    .Read_Data_2_2(ID_EX_Main_Latch_read_data_2_2), .Imm_Gen_2(ID_EX_Main_Latch_imm_gen_2),
    .ALU_Control_2(ID_EX_Main_Latch_alu_control_2), .Clock(clock_1_out), .Clear(RESET_out),
    .Write_Register(Instruction_Splitter_p5), .Write_Register_2(ID_EX_Main_Latch_write_register_2));  // open: Enable
  Multiplexer #(.select(2), .width(16), .enable("false")) multiplexer_3 (
    .in0(ID_EX_Main_Latch_read_data_1_2), .in1(Registers_p4), .in2(EX_MEM_Main_Latch_alu_result_2),
    .out(multiplexer_3_out), .sel(Forwawrding_Unit_forward_a));  // open: in3
  Multiplexer #(.select(2), .width(16), .enable("false")) multiplexer_4 (
    .in0(ID_EX_Main_Latch_read_data_2_2), .in1(Registers_p4), .in2(EX_MEM_Main_Latch_alu_result_2),
    .out(multiplexer_4_out), .sel(Forwawrding_Unit_forward_b));  // open: in3
  Multiplexer #(.width(16), .enable("false")) multiplexer_5 (
    .in0(multiplexer_4_out), .in1(ID_EX_Main_Latch_imm_gen_2), .out(multiplexer_5_out),
    .sel(ID_EX_Control_alusrc_2));
  Register #(.width(16)) register_3 (
    .D(ID_EX_Main_Latch_read_data_1_2), .en(ID_EX_Control_put_2), .Q(register_3_q), .clk(clock_1_out),
    .clr(RESET_out));
  // sixteen_bit_ALU sixteen_bit_alu_1: pin names not known; wires that end beside it: ID_EX_Main_Latch_alu_control_2, multiplexer_3_out, multiplexer_5_out, sixteen_bit_alu_1_p4
  Forwarding_Unit Forwawrding_Unit (
    .EX_MEM_RegWrite(EX_MEM_Control_regwrite_2), .EX_MEM_RegRead(EX_MEM_Main_Latch_write_register_2),
    .ID_EX_Reg1(register_1_q), .ID_EX_Reg2(register_2_q), .MEM_WB_RegWrite(Registers_p5),
    .MEM_WB_RegRead(Registers_p3), .Forward_A(Forwawrding_Unit_forward_a),
    .Forward_B(Forwawrding_Unit_forward_b));
  Hex_Digit_Display hex_digit_display_1 (.value(register_3_q[15:12]));  // open: dp
  Hex_Digit_Display hex_digit_display_2 (.value(register_3_q[11:8]));  // open: dp
  Hex_Digit_Display hex_digit_display_3 (.value(register_3_q[7:4]));  // open: dp
  Hex_Digit_Display hex_digit_display_4 (.value(register_3_q[3:0]));  // open: dp
  EX_MEM_Main_Latch EX_MEM_Main_Latch (
    .ALU_Result(sixteen_bit_alu_1_p4), .Read_Data_2(ID_EX_Main_Latch_read_data_2_2),
    .Write_Register(ID_EX_Main_Latch_write_register_2), .ALU_Result_2(EX_MEM_Main_Latch_alu_result_2),
    .Read_Data_2_2(EX_MEM_Main_Latch_read_data_2_2), .Write_Register_2(EX_MEM_Main_Latch_write_register_2),
    .Clock(clock_1_out), .Reset(RESET_out));  // open: Enable
  Control_Latch EX_MEM_Control (
    .RegWrite(ID_EX_Control_regwrite_2), .RegDst(ID_EX_Control_regdst_2), .MemRead(ID_EX_Control_memread_2),
    .MemWrite(ID_EX_Control_memwrite_2), .MemToReg(ID_EX_Control_memtoreg_2), .Halt(ID_EX_Control_halt_2),
    .RegWrite_2(EX_MEM_Control_regwrite_2), .MemRead_2(EX_MEM_Control_memread_2),
    .MemWrite_2(EX_MEM_Control_memwrite_2), .MemToReg_2(EX_MEM_Control_memtoreg_2),
    .Halt_2(EX_MEM_Control_halt_2), .Clock(clock_1_out));  // open: ALUSrc, Branch, Put, ImmSrc, RegDst_2, ALUSrc_2, Branch_2, Put_2, ImmSrc_2, Enable
  ALUtoRAM alutoram_1 (.ALU_Result(EX_MEM_Main_Latch_alu_result_2), .RAM_Address(undriven));
  RAM #(.dataWidth(16), .bus("separate")) ram_1 (
    .addr(undriven), .din(EX_MEM_Main_Latch_read_data_2_2), .data(ram_1_data),
    .str(EX_MEM_Control_memwrite_2), .sel(1'b1), .clk(clock_1_out), .ld(EX_MEM_Control_memread_2),
    .clr(RESET_out));
  Control_Latch MEM_WB_Control (
    .RegWrite(EX_MEM_Control_regwrite_2), .MemToReg(EX_MEM_Control_memtoreg_2), .Halt(EX_MEM_Control_halt_2),
    .RegWrite_2(Registers_p5), .MemToReg_2(MEM_WB_Control_memtoreg_2), .Halt_2(MEM_WB_Control_halt_2),
    .Clock(clock_1_out));  // open: RegDst, ALUSrc, MemRead, MemWrite, Branch, Put, ImmSrc, RegDst_2, ALUSrc_2, MemRead_2, MemWrite_2, Branch_2, Put_2, ImmSrc_2, Enable
  MEM_WB_Latch MRM_WB_Main_Latch (
    .Read_Data(ram_1_data), .Address(EX_MEM_Main_Latch_alu_result_2),
    .Write_Register(EX_MEM_Main_Latch_write_register_2), .Read_Data_2(MRM_WB_Main_Latch_read_data_2),
    .Address_2(MRM_WB_Main_Latch_address_2), .Write_Register_2(Registers_p3), .Clock(clock_1_out),
    .Reset(RESET_out));  // open: Enable
  Multiplexer #(.width(16), .enable("false")) multiplexer_6 (
    .in0(MRM_WB_Main_Latch_read_data_2), .in1(MRM_WB_Main_Latch_address_2), .out(Registers_p4),
    .sel(MEM_WB_Control_memtoreg_2));
  Register #(.width(1)) _1CycleWait (
    .D(MEM_WB_Control_halt_2), .Q(_1CycleWait_q), .clk(clock_1_out), .clr(RESET_out));  // open: en
  LED Halt (.in(_1CycleWait_q));
  Multiplexer multiplexer_7 ();  // open: in0, in1, out, sel, en

  // Notes on the sheet:
  //   Imp reset for control latches
  //   IF
  //   Latch Enables Needed???
  //   IS DECODER CORRECT?
  //   SHIFT??
  //   ID
  //   IMM SRC?
  //   EX
  //   VALID ALU??
  //   CORRECT ADRESS SETUP?
  //   MEM
  //   WB
endmodule
