// Logisim project 5-Stage-Pipeline-MAIN_Troubleshooting.circ as structural Verilog: 2 circuits, main circuit main
module main (
  input  [1:0] in_1,
  input  [1:0] in_2,
  output [15:0] out_3,
  output [2:0] out_4
);

  wire _1CycleWait_q, and_1_out, clock_1_out, d_ff_1_q, decoder_1_1_alusrc, decoder_1_1_branch,
       decoder_1_1_halt, decoder_1_1_immsrc, decoder_1_1_memread, decoder_1_1_memtoreg, decoder_1_1_memwrite,
       decoder_1_1_put, decoder_1_1_regdst, decoder_1_1_regwrite, EX_MEM_Control_halt_2,
       EX_MEM_Control_memread_2, EX_MEM_Control_memtoreg_2, EX_MEM_Control_memwrite_2,
       EX_MEM_Control_regwrite_2, hazard_detection_1_stall, ID_EX_Control_p13, ID_EX_Control_p14,
       ID_EX_Control_p15, ID_EX_Control_p16, ID_EX_Control_p17, ID_EX_Control_p18, ID_EX_Control_p19,
       ID_EX_Control_p20, ID_EX_Control_p21, Instruction_Splitter_p6, Instruction_Splitter_p7,
       Instruction_Splitter_p8, MEM_WB_Control_halt_2, MEM_WB_Control_memtoreg_2, not_1_out, not_2_out,
       not_3_out, not_4_out, not_5_out, Registers_p5, Registers_p10, Registers_p11, RESET_out;
  wire [2:0] EX_MEM_Main_Latch_write_register_2, ID_EX_Main_Latch_write_register_2, Instruction_Splitter_p3,
       Instruction_Splitter_p4, Instruction_Splitter_p5;
  wire [3:0] ALU_Control_aluop, ID_EX_Main_Latch_alu_control_2, Instruction_Splitter_p2;
  wire [7:0] adder_1_out, IF_ID_PC_q, multiplexer_2_out, PC_q, undriven;
  wire [15:0] EX_MEM_Main_Latch_alu_result_2, EX_MEM_Main_Latch_read_data_2_2, ID_EX_Main_Latch_imm_gen_2,
       ID_EX_Main_Latch_read_data_1_2, ID_EX_Main_Latch_read_data_2_2, IF_ID_q, MRM_WB_Main_Latch_address_2,
       MRM_WB_Main_Latch_read_data_2, multiplexer_3_out, multiplexer_4_out, multiplexer_5_out, ram_1_data,
       register_1_q, Registers_p7, Registers_p8, rom_1_data, Sign_Extender__Imm_Gen_p3, sixteen_bit_alu_1_p4;

  Multiplexer multiplexer_1 ();  // open: in0, in1, out, sel, en
  Clock clock_1 (.out(clock_1_out));
  Multiplexer #(.width(8), .enable("false")) multiplexer_2 (
    .in0(adder_1_out), .out(multiplexer_2_out), .sel(1'b0));  // open: in1
  not not_1 (not_1_out, hazard_detection_1_stall);
  Register PC (.D(multiplexer_2_out), .en(and_1_out), .Q(PC_q), .clk(clock_1_out), .clr(RESET_out));
  and and_1 (and_1_out, not_1_out, not_2_out);
  not not_2 (not_2_out, d_ff_1_q);
  Button RESET (.out(RESET_out));
  Adder adder_1 (.a(PC_q), .b(8'h1), .out(adder_1_out));  // open: cin, cout
  not not_3 (not_3_out, d_ff_1_q);
  ROM #(.dataWidth(16)) rom_1 (.addr(PC_q), .data(rom_1_data), .sel(not_3_out));
  not not_4 (not_4_out, hazard_detection_1_stall);
  Register #(.width(16)) IF_ID (.D(rom_1_data), .en(not_4_out), .Q(IF_ID_q), .clk(clock_1_out), .clr(RESET_out));
  Register IF_ID_PC (.D(PC_q), .en(not_4_out), .Q(IF_ID_PC_q), .clk(clock_1_out), .clr(RESET_out));
  // InstructionSplitter Instruction_Splitter: pin names not known; wires that end beside it: IF_ID_q, Instruction_Splitter_p2, Instruction_Splitter_p3, Instruction_Splitter_p4, Instruction_Splitter_p5, Instruction_Splitter_p6, Instruction_Splitter_p7, Instruction_Splitter_p8
  not not_5 (not_5_out, hazard_detection_1_stall);
  ALU_Control_2 ALU_Control (
    .Opcode3(Instruction_Splitter_p2[3]), .Opcode2(Instruction_Splitter_p2[2]),
    .Opcode1(Instruction_Splitter_p2[1]), .Opcode0(Instruction_Splitter_p2[0]),
    .Subop(Instruction_Splitter_p6), .Enable(not_5_out), .ALUop(ALU_Control_aluop));
  Decoder_1 decoder_1_1 (
    .Opcode3(Instruction_Splitter_p2[3]), .Opcode2(Instruction_Splitter_p2[2]),
    .Opcode1(Instruction_Splitter_p2[1]), .Opcode0(Instruction_Splitter_p2[0]),
    .Subop(Instruction_Splitter_p6), .Unisigned(Instruction_Splitter_p7), .Enable(not_5_out),
    .RegWrite(decoder_1_1_regwrite), .RegDst(decoder_1_1_regdst), .ALUSrc(decoder_1_1_alusrc),
    .MemRead(decoder_1_1_memread), .MemWrite(decoder_1_1_memwrite), .MemToReg(decoder_1_1_memtoreg),
    .Branch(decoder_1_1_branch), .Halt(decoder_1_1_halt), .Put(decoder_1_1_put), .ImmSrc(decoder_1_1_immsrc));
  // RegisterFile Registers: pin names not known; wires that end beside it: Instruction_Splitter_p3, Instruction_Splitter_p4, out_4, out_3, Registers_p5, clock_1_out, Registers_p7, Registers_p8, Instruction_Splitter_p8, Registers_p10, Registers_p11
  // SignExtend Sign_Extender__Imm_Gen: pin names not known; wires that end beside it: Instruction_Splitter_p7, Instruction_Splitter_p8, Sign_Extender__Imm_Gen_p3, IF_ID_PC_q
  Comparator #(.width(16)) comparator_1 (
    .a(Registers_p7), .b({16{1'b0}}), .gt(Registers_p10), .eq(Registers_p11));  // open: lt
  // Control_Latch ID_EX_Control: pin names not known; wires that end beside it: decoder_1_1_branch, decoder_1_1_regwrite, decoder_1_1_regdst, decoder_1_1_alusrc, decoder_1_1_memread, decoder_1_1_memwrite, decoder_1_1_memtoreg, decoder_1_1_halt, decoder_1_1_put, decoder_1_1_immsrc, 1'b1, clock_1_out, ID_EX_Control_p13, ID_EX_Control_p14, ID_EX_Control_p15, ID_EX_Control_p16, ID_EX_Control_p17, ID_EX_Control_p18, ID_EX_Control_p19, ID_EX_Control_p20, ID_EX_Control_p21
  Hazard_Detection hazard_detection_1 (
    .ID_EX_MemRead(ID_EX_Control_p16), .ID_EX_RegisterRead(ID_EX_Main_Latch_write_register_2),
    .IF_ID_RegisterR1(Instruction_Splitter_p3), .IF_ID_RegisterR2(Instruction_Splitter_p4),
    .Stall(hazard_detection_1_stall));
  ID_EX_Main_Latch ID_EX_Main_Latch (
    .Read_Data_1(Registers_p7), .Read_Data_2(Registers_p8), .Imm_Gen(Sign_Extender__Imm_Gen_p3),
    .ALU_Control(ALU_Control_aluop), .Read_Data_1_2(ID_EX_Main_Latch_read_data_1_2),
    .Read_Data_2_2(ID_EX_Main_Latch_read_data_2_2), .Imm_Gen_2(ID_EX_Main_Latch_imm_gen_2),
    .ALU_Control_2(ID_EX_Main_Latch_alu_control_2), .Enable(1'b1), .Clock(clock_1_out), .Clear(RESET_out),
    .Write_Register(Instruction_Splitter_p5), .Write_Register_2(ID_EX_Main_Latch_write_register_2));
  D_Flip_Flop d_ff_1 (.clk(ID_EX_Control_p19), .D(1'b1), .Q(d_ff_1_q));  // open: Qn, preset, en, reset
  Multiplexer #(.select(2), .width(16), .enable("false")) multiplexer_3 (
    .in0(ID_EX_Main_Latch_read_data_1_2), .in1(out_3), .in2(EX_MEM_Main_Latch_alu_result_2),
    .out(multiplexer_3_out), .sel(in_2));  // open: in3
  Multiplexer #(.select(2), .width(16), .enable("false")) multiplexer_4 (
    .in0(ID_EX_Main_Latch_read_data_2_2), .in1(out_3), .in2(EX_MEM_Main_Latch_alu_result_2),
    .out(multiplexer_4_out), .sel(in_1));  // open: in3
  Multiplexer #(.width(16), .enable("false")) multiplexer_5 (
    .in0(multiplexer_4_out), .in1(ID_EX_Main_Latch_imm_gen_2), .out(multiplexer_5_out),
    .sel(ID_EX_Control_p15));
  Register #(.width(16)) register_1 (
    .D(ID_EX_Main_Latch_read_data_1_2), .en(ID_EX_Control_p20), .Q(register_1_q), .clk(clock_1_out),
    .clr(RESET_out));
  // sixteen_bit_ALU sixteen_bit_alu_1: pin names not known; wires that end beside it: ID_EX_Main_Latch_alu_control_2, multiplexer_3_out, multiplexer_5_out, sixteen_bit_alu_1_p4
  Hex_Digit_Display hex_digit_display_1 (.value(register_1_q[15:12]));  // open: dp
  Hex_Digit_Display hex_digit_display_2 (.value(register_1_q[11:8]));  // open: dp
  Hex_Digit_Display hex_digit_display_3 (.value(register_1_q[3:0]));  // open: dp
  Hex_Digit_Display hex_digit_display_4 (.value(register_1_q[7:4]));  // open: dp
  EX_MEM_Main_Latch EX_MEM_Main_Latch (
    .ALU_Result(sixteen_bit_alu_1_p4), .Read_Data_2(ID_EX_Main_Latch_read_data_2_2),
    .Write_Register(ID_EX_Main_Latch_write_register_2), .ALU_Result_2(EX_MEM_Main_Latch_alu_result_2),
    .Read_Data_2_2(EX_MEM_Main_Latch_read_data_2_2), .Write_Register_2(EX_MEM_Main_Latch_write_register_2),
    .Enable(1'b1), .Clock(clock_1_out), .Reset(RESET_out));
  Control_Latch EX_MEM_Control (
    .RegWrite(ID_EX_Control_p13), .RegDst(ID_EX_Control_p14), .MemRead(ID_EX_Control_p16),
    .MemWrite(ID_EX_Control_p17), .MemToReg(ID_EX_Control_p18), .Halt(ID_EX_Control_p19),
    .RegWrite_2(EX_MEM_Control_regwrite_2), .MemRead_2(EX_MEM_Control_memread_2),
    .MemWrite_2(EX_MEM_Control_memwrite_2), .MemToReg_2(EX_MEM_Control_memtoreg_2),
    .Halt_2(EX_MEM_Control_halt_2), .Enable(1'b1), .Clock(clock_1_out));  // open: ALUSrc, Branch, Put, ImmSrc, RegDst_2, ALUSrc_2, Branch_2, Put_2, ImmSrc_2
  ALUtoRAM alutoram_1 (.ALU_Result(EX_MEM_Main_Latch_alu_result_2), .RAM_Address(undriven));
  RAM #(.dataWidth(16), .bus("separate")) ram_1 (
    .addr(undriven), .din(EX_MEM_Main_Latch_read_data_2_2), .data(ram_1_data),
    .str(EX_MEM_Control_memwrite_2), .sel(1'b1), .clk(clock_1_out), .ld(EX_MEM_Control_memread_2),
    .clr(RESET_out));
  Control_Latch MEM_WB_Control (
    .RegWrite(EX_MEM_Control_regwrite_2), .MemToReg(EX_MEM_Control_memtoreg_2), .Halt(EX_MEM_Control_halt_2),
    .RegWrite_2(Registers_p5), .MemToReg_2(MEM_WB_Control_memtoreg_2), .Halt_2(MEM_WB_Control_halt_2),
    .Enable(1'b1), .Clock(clock_1_out));  // open: RegDst, ALUSrc, MemRead, MemWrite, Branch, Put, ImmSrc, RegDst_2, ALUSrc_2, MemRead_2, MemWrite_2, Branch_2, Put_2, ImmSrc_2
  MEM_WB_Latch MRM_WB_Main_Latch (
    .Read_Data(ram_1_data), .Address(EX_MEM_Main_Latch_alu_result_2),
    .Write_Register(EX_MEM_Main_Latch_write_register_2), .Read_Data_2(MRM_WB_Main_Latch_read_data_2),
    .Address_2(MRM_WB_Main_Latch_address_2), .Write_Register_2(out_4), .Enable(1'b1), .Clock(clock_1_out),
    .Reset(RESET_out));
  Multiplexer #(.width(16), .enable("false")) multiplexer_6 (
    .in0(MRM_WB_Main_Latch_address_2), .in1(MRM_WB_Main_Latch_read_data_2), .out(out_3),
    .sel(MEM_WB_Control_memtoreg_2));
  Register #(.width(1)) _1CycleWait (
    .D(MEM_WB_Control_halt_2), .en(1'b1), .Q(_1CycleWait_q), .clk(clock_1_out), .clr(RESET_out));
  Register #(.width(16)) register_2 (.D(out_3), .clk(clock_1_out), .clr(1'b1));  // open: en, Q
  Register #(.width(3)) register_3 (.D(out_4), .clr(1'b1));  // open: en, Q, clk
  LED Halt (.in(_1CycleWait_q));
  Multiplexer multiplexer_7 ();  // open: in0, in1, out, sel, en

  // Notes on the sheet:
  //   addi
  //   addui
  //   halt
  //   IF
  //   contents of rom_1 (hex, n*v repeats v):
  //   1301 1520 6281 f200
  //   ID
  //   IMM SRC?
  //   EX
  //   VALID ALU??
  //   CORRECT ADRESS SETUP?
  //   MEM
  //   WB
endmodule

module TESTS (
  input  _3,
  input  _2,
  input  _1,
  input  _0,
  input  SubOP,
  input  [15:0] A,
  input  [15:0] B,
  output [3:0] out_8,
  output [15:0] result
);

  ALU_Control_2 alu_control_2_1 (
    .Opcode3(_3), .Opcode2(_2), .Opcode1(_1), .Opcode0(_0), .Subop(SubOP), .ALUop(out_8));  // open: Enable
  // sixteen_bit_ALU sixteen_bit_alu_1: pin names not known; wires that end beside it: out_8, A, B, result
endmodule
