// Logisim project Control_Latch.circ as structural Verilog: 1 circuit, main circuit Control Latch
module Control_Latch (
  input  Enable,
  input  Clock,
  input  RegWrite,
  input  RegDst,
  input  ALUSrc,
  input  MemRead,
  input  MemWrite,
  input  MemToReg,
  input  Branch,
  input  Halt,
  input  Put,
  input  ImmSrc,
  output RegWrite_2,
  output RegDst_2,
  output ALUSrc_2,
  output MemRead_2,
  output MemWrite_2,
  output MemToReg_2,
  output Branch_2,
  output Halt_2,
  output Put_2,
  output ImmSrc_2
);

  Register #(.width(1)) register_1 (.D(RegWrite), .en(Enable), .Q(RegWrite_2), .clk(Clock));  // open: clr
  Register #(.width(1)) register_2 (.D(RegDst), .en(Enable), .Q(RegDst_2), .clk(Clock));  // open: clr
  Register #(.width(1)) register_3 (.D(ALUSrc), .en(Enable), .Q(ALUSrc_2), .clk(Clock));  // open: clr
  Register #(.width(1)) register_4 (.D(MemRead), .en(Enable), .Q(MemRead_2), .clk(Clock));  // open: clr
  Register #(.width(1)) register_5 (.D(MemWrite), .en(Enable), .Q(MemWrite_2), .clk(Clock));  // open: clr
  Register #(.width(1)) register_6 (.D(MemToReg), .en(Enable), .Q(MemToReg_2), .clk(Clock));  // open: clr
  Register #(.width(1)) register_7 (.D(Branch), .en(Enable), .Q(Branch_2), .clk(Clock));  // open: clr
  Register #(.width(1)) register_8 (.D(Halt), .en(Enable), .Q(Halt_2), .clk(Clock));  // open: clr
  Register #(.width(1)) register_9 (.D(Put), .en(Enable), .Q(Put_2), .clk(Clock));  // open: clr
  Register #(.width(1)) register_10 (.D(ImmSrc), .en(Enable), .Q(ImmSrc_2), .clk(Clock));  // open: clr
endmodule
