// Logisim project SubCircuits.circ as structural Verilog
module Register (
  input  [2:0] ReadRegister1,
  input  [2:0] ReadRegister2,
  input  [2:0] WriteRegister,
  input  [15:0] WriteData,
  input  WriteEnable,
  input  Clock,
  output [15:0] ReadData1,
  output [15:0] ReadData2
);

  wire decoder_1_out0, decoder_1_out1, decoder_1_out2, decoder_1_out3, decoder_1_out4, decoder_1_out5,
       decoder_1_out6, decoder_1_out7;
  wire [15:0] r0_q, r1_q, r2_q, r3_q, r4_q, r5_q, r6_q, r7_q;

  Decoder_part #(.select(3), .disabled(0)) decoder_1 (
    .out0(decoder_1_out0), .out1(decoder_1_out1), .out2(decoder_1_out2), .out3(decoder_1_out3),
    .out4(decoder_1_out4), .out5(decoder_1_out5), .out6(decoder_1_out6), .out7(decoder_1_out7),
    .sel(WriteRegister), .en(WriteEnable));
  Register_part #(.width(16)) r0 (.D(WriteData), .en(decoder_1_out0), .Q(r0_q), .clk(Clock));  // open: clr
  Register_part #(.width(16)) r1 (.D(WriteData), .en(decoder_1_out1), .Q(r1_q), .clk(Clock));  // open: clr
  Register_part #(.width(16)) r2 (.D(WriteData), .en(decoder_1_out2), .Q(r2_q), .clk(Clock));  // open: clr
  Register_part #(.width(16)) r3 (.D(WriteData), .en(decoder_1_out3), .Q(r3_q), .clk(Clock));  // open: clr
  Register_part #(.width(16)) r4 (.D(WriteData), .en(decoder_1_out4), .Q(r4_q), .clk(Clock));  // open: clr
  Register_part #(.width(16)) r5 (.D(WriteData), .en(decoder_1_out5), .Q(r5_q), .clk(Clock));  // open: clr
  Register_part #(.width(16)) r6 (.D(WriteData), .en(decoder_1_out6), .Q(r6_q), .clk(Clock));  // open: clr
  Register_part #(.width(16)) r7 (.D(WriteData), .en(decoder_1_out7), .Q(r7_q), .clk(Clock));  // open: clr
  Multiplexer #(.select(3), .width(16), .enable("false")) multiplexer_1 (
    .in0(r0_q), .in1(r1_q), .in2(r2_q), .in3(r3_q), .in4(r4_q), .in5(r5_q), .in6(r6_q), .in7(r7_q),
    .out(ReadData1), .sel(ReadRegister1));
  Multiplexer #(.select(3), .width(16), .enable("false")) multiplexer_2 (
    .in0(r0_q), .in1(r1_q), .in2(r2_q), .in3(r3_q), .in4(r4_q), .in5(r5_q), .in6(r6_q), .in7(r7_q),
    .out(ReadData2), .sel(ReadRegister2));
endmodule

module Decoder (
);

  Decoder_1 Decoder_1 ();  // open: Opcode3, Opcode2, Opcode1, Opcode0, Subop, Unisigned, Enable, RegWrite, RegDst, ALUSrc, MemRead, MemWrite, MemToReg, Branch, Halt, Put, ImmSrc
  Decoder_2_ALU Decoder_2_ALU ();  // open: Opcode3, Opcode2, Opcode1, Opcode0, Subop, Enable, ALUOP
endmodule

module Decoder_1 (
  input  Enable,
  input  Opcode3,
  input  Opcode2,
  input  Opcode1,
  input  Opcode0,
  input  Subop,
  input  Unisigned,
  output RegWrite,
  output RegDst,
  output ALUSrc,
  output MemRead,
  output MemWrite,
  output MemToReg,
  output Branch,
  output Halt,
  output Put,
  output ImmSrc
);

  wire and_1_out, and_2_out, and_3_out, and_4_out, and_5_out, and_6_out, and_7_out, and_8_out, and_9_out,
       and_10_out, and_11_out, and_12_out, and_13_out, and_14_out, and_15_out, and_16_out, not_1_out,
       not_2_out, not_3_out, not_4_out, not_5_out, not_6_out, not_7_out, not_8_out, not_9_out, not_10_out,
       not_11_out, not_12_out, not_13_out, not_14_out, not_15_out, not_16_out, not_17_out, not_18_out,
       not_19_out, not_20_out, not_21_out, not_22_out, not_23_out, not_24_out, not_25_out, not_26_out,
       not_27_out, not_28_out, not_29_out, not_30_out, not_31_out, not_32_out, not_33_out, not_34_out,
       not_35_out, not_36_out, not_37_out, not_38_out, not_39_out, not_40_out, not_41_out, not_42_out,
       or_1_out, or_2_out, or_3_out;

  not not_1 (not_1_out, Opcode3);
  not not_2 (not_2_out, Opcode2);
  not not_3 (not_3_out, Opcode1);
  not not_4 (not_4_out, Subop);
  not not_5 (not_5_out, Opcode3);
  not not_6 (not_6_out, Opcode2);
  not not_7 (not_7_out, Opcode1);
  not not_8 (not_8_out, Opcode3);
  not not_9 (not_9_out, Opcode0);
  not not_10 (not_10_out, Subop);
  not not_11 (not_11_out, Opcode3);
  not not_12 (not_12_out, Opcode2);
  not not_13 (not_13_out, Opcode0);
  not not_14 (not_14_out, Subop);
  not not_15 (not_15_out, Opcode3);
  not not_16 (not_16_out, Opcode2);
  not not_17 (not_17_out, Opcode1);
  not not_18 (not_18_out, Opcode3);
  not not_19 (not_19_out, Opcode0);
  not not_20 (not_20_out, Subop);
  not not_21 (not_21_out, Opcode2);
  not not_22 (not_22_out, Opcode0);
  not not_23 (not_23_out, Opcode3);
  not not_24 (not_24_out, Opcode2);
  not not_25 (not_25_out, Opcode1);
  not not_26 (not_26_out, Opcode3);
  not not_27 (not_27_out, Opcode0);
  not not_28 (not_28_out, Subop);
  not not_29 (not_29_out, Opcode3);
  not not_30 (not_30_out, Opcode0);
  not not_31 (not_31_out, Opcode3);
  not not_32 (not_32_out, Opcode0);
  not not_33 (not_33_out, Subop);
  not not_34 (not_34_out, Opcode2);
  not not_35 (not_35_out, Opcode0);
  not not_36 (not_36_out, Opcode3);
  not not_37 (not_37_out, Subop);
  and and_1 (and_1_out, Opcode3, Opcode2, Opcode1, Opcode0);
  not not_38 (not_38_out, Opcode3);
  not not_39 (not_39_out, Opcode2);
  not not_40 (not_40_out, Opcode1);
  not not_41 (not_41_out, Opcode2);
  not not_42 (not_42_out, Opcode0);
  and and_2 (and_2_out, not_1_out, not_2_out, not_3_out, not_4_out);
  and and_3 (and_3_out, not_5_out, not_6_out, not_7_out, Opcode0);
  and and_4 (and_4_out, not_8_out, Opcode1, not_9_out, not_10_out);
  and and_5 (and_5_out, not_11_out, not_12_out, not_13_out, not_14_out);
  and and_6 (and_6_out, not_15_out, not_16_out, not_17_out, Opcode0);
  and and_7 (and_7_out, not_18_out, Opcode1, not_19_out, not_20_out);
  and and_8 (and_8_out, Opcode3, not_21_out, not_22_out, Unisigned);
  and and_9 (and_9_out, not_23_out, not_24_out, not_25_out, Opcode0);
  and and_10 (and_10_out, not_26_out, Opcode2, Opcode1, not_27_out, not_28_out);
  and and_11 (and_11_out, not_29_out, Opcode2, Opcode1, not_30_out, Subop);
  and and_12 (and_12_out, not_31_out, Opcode2, Opcode1, not_32_out, not_33_out);
  and and_13 (and_13_out, Opcode3, not_34_out, not_35_out, Unisigned);
  and and_14 (and_14_out, not_36_out, Opcode2, Opcode1, Opcode0, not_37_out);
  and and_15 (and_15_out, not_38_out, not_39_out, not_40_out, Opcode0, Unisigned);
  and and_16 (and_16_out, Opcode3, not_41_out, not_42_out, Unisigned);
  or or_1 (or_1_out, and_2_out, and_3_out, and_4_out);
  or or_2 (or_2_out, and_5_out, and_6_out, and_7_out, and_8_out);
  or or_3 (or_3_out, and_15_out, and_16_out);
  and and_17 (RegWrite, or_1_out, Enable);
  and and_18 (RegDst, or_2_out, Enable);
  and and_19 (ALUSrc, and_9_out, Enable);
  and and_20 (MemRead, and_10_out, Enable);
  and and_21 (MemWrite, and_11_out, Enable);
  and and_22 (MemToReg, and_12_out, Enable);
  and and_23 (Branch, and_13_out, Enable);
  and and_24 (Halt, and_14_out, Enable);
  and and_25 (Put, and_1_out, Enable);
  and and_26 (ImmSrc, or_3_out, Enable);
endmodule

module Decoder_2_ALU (
  input  Opcode3,
  input  Opcode2,
  input  Enable,
  input  Opcode1,
  input  Opcode0,
  input  Subop,
  output [3:0] ALUOP
);

  wire and_4_out, and_5_out, not_1_out, not_2_out, not_3_out, not_4_out, not_5_out, not_6_out, not_7_out,
       not_8_out, not_9_out, not_10_out, not_11_out, not_12_out, not_13_out, not_14_out;
  wire [1:1] and_1_out;
  wire [3:0] or_2_out;
  wire [3:1] and_2_out;

  not not_1 (not_1_out, Opcode2);
  and and_1 (and_1_out[1], Opcode3, not_1_out);
  not not_2 (not_2_out, Opcode3);
  not not_3 (not_3_out, Opcode2);
  not not_4 (not_4_out, Subop);
  not not_5 (not_5_out, Opcode3);
  not not_6 (not_6_out, Opcode2);
  not not_7 (not_7_out, Opcode1);
  not not_8 (not_8_out, Opcode0);
  not not_9 (not_9_out, Opcode3);
  not not_10 (not_10_out, Opcode2);
  not not_11 (not_11_out, Subop);
  not not_12 (not_12_out, Opcode3);
  and and_2 (and_2_out[1], not_12_out, not_13_out, not_14_out);
  not not_13 (not_13_out, Opcode2);
  not not_14 (not_14_out, Opcode1);
  and and_3 (and_2_out[3], not_2_out, not_3_out, Opcode1, Opcode0, not_4_out);
  and and_4 (and_4_out, not_5_out, not_6_out, not_7_out, not_8_out, Subop);
  or or_1 (and_2_out[2], and_4_out, and_5_out);
  and and_5 (and_5_out, not_9_out, not_10_out, Opcode1, Opcode0, not_11_out);
  assign or_2_out = {and_2_out, 1'b0} | {2'b00, and_1_out[1], 1'b0};  // OR_Gate or_2, 4 bits wide
  assign ALUOP = Enable ? or_2_out : 4'bz;  // Controlled_Buffer controlled_buffer_1
endmodule

module Hex_Display (
);

  Register_part #(.width(16)) register_1 ();  // open: D, en, Q, clk, clr
  Hex_Digit_Display hex_digit_display_1 ();  // open: value, dp
  Hex_Digit_Display hex_digit_display_2 ();  // open: value, dp
  Hex_Digit_Display hex_digit_display_3 ();  // open: value, dp
  Hex_Digit_Display hex_digit_display_4 ();  // open: value, dp
endmodule

module ID_EX_Main_Latch (
  input  Enable,
  input  Clock,
  input  Clear,
  input  [15:0] Read_Data_1,
  input  [15:0] Read_Data_2,
  input  [15:0] Imm_Gen,
  input  [2:0] Write_Register,
  input  [3:0] ALU_Control,
  output [15:0] Read_Data_1_2,
  output [15:0] Read_Data_2_2,
  output [15:0] Imm_Gen_2,
  output [2:0] Write_Register_2,
  output [3:0] ALU_Control_2
);

  Register_part #(.width(16)) Read_Data1 (.D(Read_Data_1), .en(Enable), .Q(Read_Data_1_2), .clk(Clock), .clr(Clear));
  Register_part #(.width(16)) Read_Data2 (.D(Read_Data_2), .en(Enable), .Q(Read_Data_2_2), .clk(Clock), .clr(Clear));
  Register_part #(.width(16)) u_Imm_Gen (.D(Imm_Gen), .en(Enable), .Q(Imm_Gen_2), .clk(Clock), .clr(Clear));
  Register_part #(.width(3)) u_Write_Register (
    .D(Write_Register), .en(Enable), .Q(Write_Register_2), .clk(Clock), .clr(Clear));
  Register_part #(.width(4)) u_ALU_Control (.D(ALU_Control), .en(Enable), .Q(ALU_Control_2), .clk(Clock), .clr(Clear));
endmodule

module EX_MEM_Main_Latch (
  input  Enable,
  input  Clock,
  input  Reset,
  input  [15:0] ALU_Result,
  input  [15:0] Read_Data_2,
  input  [2:0] Write_Register,
  output [15:0] ALU_Result_2,
  output [15:0] Read_Data_2_2,
  output [2:0] Write_Register_2
);

  Register_part #(.width(16)) u_ALU_Result (.D(ALU_Result), .en(Enable), .Q(ALU_Result_2), .clk(Clock), .clr(Reset));
  Register_part #(.width(16)) u_Read_Data_2 (.D(Read_Data_2), .en(Enable), .Q(Read_Data_2_2), .clk(Clock), .clr(Reset));
  Register_part #(.width(3)) u_Write_Register (
    .D(Write_Register), .en(Enable), .Q(Write_Register_2), .clk(Clock), .clr(Reset));
endmodule

module ALUtoRAM (
  input  [15:0] ALU_Result,
  input  [7:0] RAM_Address
);


  assign RAM_Address = ALU_Result[7:0];
endmodule

module MEM_WB_Latch (
  input  Enable,
  input  Clock,
  input  Reset,
  input  [15:0] Read_Data,
  input  [15:0] Address,
  input  [2:0] Write_Register,
  output [15:0] Read_Data_2,
  output [15:0] Address_2,
  output [2:0] Write_Register_2
);

  Register_part #(.width(16)) u_Read_Data (.D(Read_Data), .en(Enable), .Q(Read_Data_2), .clk(Clock), .clr(Reset));
  Register_part #(.width(16)) Adress (.D(Address), .en(Enable), .Q(Address_2), .clk(Clock), .clr(Reset));
  Register_part #(.width(3)) u_Write_Register (
    .D(Write_Register), .en(Enable), .Q(Write_Register_2), .clk(Clock), .clr(Reset));
endmodule

module Forwarding_Unit (
  input  EX_MEM_RegWrite,
  input  [2:0] EX_MEM_RegRead,
  input  [2:0] ID_EX_Reg1,
  input  [2:0] ID_EX_Reg2,
  input  MEM_WB_RegWrite,
  input  [2:0] MEM_WB_RegRead,
  output [1:0] Forward_A,
  output [1:0] Forward_B
);

  wire comparator_1_eq, comparator_2_eq, comparator_3_eq, comparator_4_eq, comparator_5_eq, comparator_6_eq,
       comparator_7_eq, comparator_8_eq, not_1_out, not_2_out, not_3_out, not_4_out;

  Comparator #(.width(3)) comparator_1 (.a(EX_MEM_RegRead), .b(3'b000), .eq(comparator_1_eq));  // open: gt, lt
  Comparator #(.width(3)) comparator_2 (.a(EX_MEM_RegRead), .b(ID_EX_Reg1), .eq(comparator_2_eq));  // open: gt, lt
  Comparator #(.width(3)) comparator_3 (.a(EX_MEM_RegRead), .b(3'b000), .eq(comparator_3_eq));  // open: gt, lt
  Comparator #(.width(3)) comparator_4 (.a(EX_MEM_RegRead), .b(ID_EX_Reg2), .eq(comparator_4_eq));  // open: gt, lt
  Comparator #(.width(3)) comparator_5 (.a(MEM_WB_RegRead), .b(3'b000), .eq(comparator_5_eq));  // open: gt, lt
  not not_1 (not_1_out, comparator_5_eq);
  Comparator #(.width(3)) comparator_6 (.a(MEM_WB_RegRead), .b(ID_EX_Reg1), .eq(comparator_6_eq));  // open: gt, lt
  not not_2 (not_2_out, comparator_7_eq);
  Comparator #(.width(3)) comparator_7 (.a(MEM_WB_RegRead), .b(3'b000), .eq(comparator_7_eq));  // open: gt, lt
  Comparator #(.width(3)) comparator_8 (.a(MEM_WB_RegRead), .b(ID_EX_Reg2), .eq(comparator_8_eq));  // open: gt, lt
  not not_3 (not_3_out, comparator_1_eq);
  not not_4 (not_4_out, comparator_3_eq);
  and and_1 (Forward_A[1], EX_MEM_RegWrite, not_3_out, comparator_2_eq);
  and and_2 (Forward_B[1], EX_MEM_RegWrite, not_4_out, comparator_4_eq);
  and and_3 (Forward_A[0], MEM_WB_RegWrite, not_1_out, comparator_6_eq);
  and and_4 (Forward_B[0], MEM_WB_RegWrite, not_2_out, comparator_8_eq);

  // Notes on the sheet:
  //   MEM Hazard
  //   EX HAZARD
  //   A10
  //   B10
  //   A01
  //   B01
endmodule

module Hazard_Detection (
  input  ID_EX_MemRead,
  input  [2:0] ID_EX_RegisterRead,
  input  [2:0] IF_ID_RegisterR1,
  input  [2:0] IF_ID_RegisterR2,
  output Stall
);

  wire comparator_1_eq, comparator_2_eq, or_1_out;

  Comparator #(.width(3)) comparator_1 (
    .a(ID_EX_RegisterRead), .b(IF_ID_RegisterR1), .eq(comparator_1_eq));  // open: gt, lt
  Comparator #(.width(3)) comparator_2 (
    .a(ID_EX_RegisterRead), .b(IF_ID_RegisterR2), .eq(comparator_2_eq));  // open: gt, lt
  or or_1 (or_1_out, comparator_1_eq, comparator_2_eq);
  and and_1 (Stall, ID_EX_MemRead, or_1_out);
endmodule

module ALU_Control (
  input  Opcode3,
  input  Opcode2,
  input  Opcode1,
  input  Opcode0,
  input  Subop,
  output ALUOP3,
  output ALUOP2,
  output ALUOP1,
  output ALUOP0
);


  assign ALUOP0 = 1'b0;
  assign ALUOP1 = 1'b1;
  assign ALUOP2 = Opcode1;
  assign ALUOP3 = 1'b0;
endmodule

module ALU_Control_2 (
  input  Enable,
  input  Opcode3,
  input  Opcode2,
  input  Opcode1,
  input  Opcode0,
  input  Subop,
  output [3:0] ALUop
);

  assign ALUop = Enable ? {1'b0, Opcode1, 2'b10} : 4'bz;  // Controlled_Buffer controlled_buffer_1
endmodule
