// Logisim project forwarding_unit.circ as structural Verilog
module Register (
  input  [2:0] ReadRegister1,
  input  [2:0] ReadRegister2,
  input  [2:0] WriteRegister,
  input  [15:0] WriteData,
  input  WriteEnable,
  input  Clock,
  output [15:0] ReadData1,
  output [15:0] ReadData2
);

  wire decoder_1_out0, decoder_1_out1, decoder_1_out2, decoder_1_out3, decoder_1_out4, decoder_1_out5,
       decoder_1_out6, decoder_1_out7;
  wire [15:0] r0_q, r1_q, r2_q, r3_q, r4_q, r5_q, r6_q, r7_q;

  Decoder_part #(.select(3), .disabled(0)) decoder_1 (
    .out0(decoder_1_out0), .out1(decoder_1_out1), .out2(decoder_1_out2), .out3(decoder_1_out3),
    .out4(decoder_1_out4), .out5(decoder_1_out5), .out6(decoder_1_out6), .out7(decoder_1_out7),
    .sel(WriteRegister), .en(WriteEnable));
  Register_part #(.width(16)) r0 (.D(WriteData), .en(decoder_1_out0), .Q(r0_q), .clk(Clock));  // open: clr
  Register_part #(.width(16)) r1 (.D(WriteData), .en(decoder_1_out1), .Q(r1_q), .clk(Clock));  // open: clr
  Register_part #(.width(16)) r2 (.D(WriteData), .en(decoder_1_out2), .Q(r2_q), .clk(Clock));  // open: clr
  Register_part #(.width(16)) r3 (.D(WriteData), .en(decoder_1_out3), .Q(r3_q), .clk(Clock));  // open: clr
  Register_part #(.width(16)) r4 (.D(WriteData), .en(decoder_1_out4), .Q(r4_q), .clk(Clock));  // open: clr
  Register_part #(.width(16)) r5 (.D(WriteData), .en(decoder_1_out5), .Q(r5_q), .clk(Clock));  // open: clr
  Register_part #(.width(16)) r6 (.D(WriteData), .en(decoder_1_out6), .Q(r6_q), .clk(Clock));  // open: clr
  Register_part #(.width(16)) r7 (.D(WriteData), .en(decoder_1_out7), .Q(r7_q), .clk(Clock));  // open: clr
  Multiplexer #(.select(3), .width(16), .enable("false")) multiplexer_1 (
    .in0(r0_q), .in1(r1_q), .in2(r2_q), .in3(r3_q), .in4(r4_q), .in5(r5_q), .in6(r6_q), .in7(r7_q),
    .out(ReadData1), .sel(ReadRegister1));
  Multiplexer #(.select(3), .width(16), .enable("false")) multiplexer_2 (
    .in0(r0_q), .in1(r1_q), .in2(r2_q), .in3(r3_q), .in4(r4_q), .in5(r5_q), .in6(r6_q), .in7(r7_q),
    .out(ReadData2), .sel(ReadRegister2));
endmodule

module Decoder (
);

  Decoder_1 Decoder_1 ();  // open: Opcode3, Opcode2, Opcode1, Opcode0, Subop, Unisigned, RegWrite, RegDst, ALUSrc, MemRead, MemWrite, MemToReg, Branch, Halt, Put, ImmSrc
  Decoder_2_ALU Decoder_2_ALU ();  // open: Opcode3, Opcode2, Opcode1, Opcode0, Subop, ALUOp1, ALUOp2
endmodule

module Decoder_1 (
  input  Opcode3,
  input  Opcode2,
  input  Opcode1,
  input  Opcode0,
  input  Subop,
  input  Unisigned,
  output RegWrite,
  output RegDst,
  output ALUSrc,
  output MemRead,
  output MemWrite,
  output MemToReg,
  output Branch,
  output Halt,
  output Put,
  output ImmSrc
);

  wire and_2_out, and_3_out, and_4_out, and_5_out, and_6_out, and_7_out, and_8_out, and_15_out, and_16_out,
       not_1_out, not_2_out, not_3_out, not_4_out, not_5_out, not_6_out, not_7_out, not_8_out, not_9_out,
       not_10_out, not_11_out, not_12_out, not_13_out, not_14_out, not_15_out, not_16_out, not_17_out,
       not_18_out, not_19_out, not_20_out, not_21_out, not_22_out, not_23_out, not_24_out, not_25_out,
       not_26_out, not_27_out, not_28_out, not_29_out, not_30_out, not_31_out, not_32_out, not_33_out,
       not_34_out, not_35_out, not_36_out, not_37_out, not_38_out, not_39_out, not_40_out, not_41_out,
       not_42_out;

  not not_1 (not_1_out, Opcode3);
  not not_2 (not_2_out, Opcode2);
  not not_3 (not_3_out, Opcode1);
  not not_4 (not_4_out, Subop);
  not not_5 (not_5_out, Opcode3);
  not not_6 (not_6_out, Opcode2);
  not not_7 (not_7_out, Opcode1);
  not not_8 (not_8_out, Opcode3);
  not not_9 (not_9_out, Opcode0);
  not not_10 (not_10_out, Subop);
  not not_11 (not_11_out, Opcode3);
  not not_12 (not_12_out, Opcode2);
  not not_13 (not_13_out, Opcode0);
  not not_14 (not_14_out, Subop);
  not not_15 (not_15_out, Opcode3);
  not not_16 (not_16_out, Opcode2);
  not not_17 (not_17_out, Opcode1);
  not not_18 (not_18_out, Opcode3);
  not not_19 (not_19_out, Opcode0);
  not not_20 (not_20_out, Subop);
  not not_21 (not_21_out, Opcode2);
  not not_22 (not_22_out, Opcode0);
  not not_23 (not_23_out, Opcode3);
  not not_24 (not_24_out, Opcode2);
  not not_25 (not_25_out, Opcode1);
  not not_26 (not_26_out, Opcode3);
  not not_27 (not_27_out, Opcode0);
  not not_28 (not_28_out, Subop);
  not not_29 (not_29_out, Opcode3);
  not not_30 (not_30_out, Opcode0);
  not not_31 (not_31_out, Opcode3);
  not not_32 (not_32_out, Opcode0);
  not not_33 (not_33_out, Subop);
  not not_34 (not_34_out, Opcode2);
  not not_35 (not_35_out, Opcode0);
  not not_36 (not_36_out, Opcode3);
  not not_37 (not_37_out, Subop);
  and and_1 (Put, Opcode3, Opcode2, Opcode1, Opcode0);
  not not_38 (not_38_out, Opcode3);
  not not_39 (not_39_out, Opcode2);
  not not_40 (not_40_out, Opcode1);
  not not_41 (not_41_out, Opcode2);
  not not_42 (not_42_out, Opcode0);
  and and_2 (and_2_out, not_1_out, not_2_out, not_3_out, not_4_out);
  and and_3 (and_3_out, not_5_out, not_6_out, not_7_out, Opcode0);
  and and_4 (and_4_out, not_8_out, Opcode1, not_9_out, not_10_out);
  and and_5 (and_5_out, not_11_out, not_12_out, not_13_out, not_14_out);
  and and_6 (and_6_out, not_15_out, not_16_out, not_17_out, Opcode0);
  and and_7 (and_7_out, not_18_out, Opcode1, not_19_out, not_20_out);
  and and_8 (and_8_out, Opcode3, not_21_out, not_22_out, Unisigned);
  and and_9 (ALUSrc, not_23_out, not_24_out, not_25_out, Opcode0);
  and and_10 (MemRead, not_26_out, Opcode2, Opcode1, not_27_out, not_28_out);
  and and_11 (MemWrite, not_29_out, Opcode2, Opcode1, not_30_out, Subop);
  and and_12 (MemToReg, not_31_out, Opcode2, Opcode1, not_32_out, not_33_out);
  and and_13 (Branch, Opcode3, not_34_out, not_35_out, Unisigned);
  and and_14 (Halt, not_36_out, Opcode2, Opcode1, Opcode0, not_37_out);
  and and_15 (and_15_out, not_38_out, not_39_out, not_40_out, Opcode0, Unisigned);
  and and_16 (and_16_out, Opcode3, not_41_out, not_42_out, Unisigned);
  or or_1 (RegWrite, and_2_out, and_3_out, and_4_out);
  or or_2 (RegDst, and_5_out, and_6_out, and_7_out, and_8_out);
  or or_3 (ImmSrc, and_15_out, and_16_out);
endmodule

module Decoder_2_ALU (
  input  Opcode3,
  input  Opcode2,
  input  Opcode1,
  input  Opcode0,
  input  Subop,
  output ALUOp1,
  output ALUOp2
);

  wire and_2_out, and_3_out, not_1_out, not_2_out, not_3_out, not_4_out, not_5_out, not_6_out, not_7_out;

  not not_1 (not_1_out, Opcode2);
  not not_2 (not_2_out, Opcode0);
  not not_3 (not_3_out, Opcode2);
  not not_4 (not_4_out, Opcode0);
  not not_5 (not_5_out, Subop);
  not not_6 (not_6_out, Opcode2);
  not not_7 (not_7_out, Opcode0);
  and and_1 (ALUOp1, Opcode3, not_1_out, not_2_out);
  and and_2 (and_2_out, not_3_out, Opcode1, not_4_out, not_5_out);
  and and_3 (and_3_out, Opcode3, not_6_out, Opcode1, not_7_out);
  or or_1 (ALUOp2, and_2_out, and_3_out);
endmodule

module Hex_Display (
);

  Register_part #(.width(16)) register_1 ();  // open: D, en, Q, clk, clr
  Hex_Digit_Display hex_digit_display_1 ();  // open: value, dp
  Hex_Digit_Display hex_digit_display_2 ();  // open: value, dp
  Hex_Digit_Display hex_digit_display_3 ();  // open: value, dp
  Hex_Digit_Display hex_digit_display_4 ();  // open: value, dp
endmodule

module forwarding_unit (
  input  [2:0] rs1,
  input  [2:0] rd_EM_MEM,
  input  [2:0] rd_MEM_WB,
  input  [2:0] rs2,
  input  RegWrite_EX_MEM,
  input  RegWrite_MEM_WB,
  output FowardA,
  output FowardB
);

  wire and_1_out, and_2_out, and_3_out, and_4_out, not_1_out, not_2_out, not_3_out, not_4_out, or_1_out,
       or_2_out, or_3_out, or_4_out, xor_1_out, xor_2_out, xor_3_out, xor_4_out, xor_5_out, xor_6_out,
       xor_7_out, xor_8_out, xor_9_out, xor_10_out, xor_11_out, xor_12_out;

  xor xor_1 (xor_1_out, rs1[0], rd_EM_MEM[0]);
  xor xor_2 (xor_2_out, rs1[1], rd_EM_MEM[1]);
  xor xor_3 (xor_3_out, rs1[2], rd_EM_MEM[2]);
  xor xor_4 (xor_4_out, rs1[0], rd_MEM_WB[0]);
  xor xor_5 (xor_5_out, rs1[1], rd_MEM_WB[1]);
  xor xor_6 (xor_6_out, rs1[2], rd_MEM_WB[2]);
  xor xor_7 (xor_7_out, rs2[0], rd_EM_MEM[0]);
  xor xor_8 (xor_8_out, rs2[1], rd_EM_MEM[1]);
  xor xor_9 (xor_9_out, rs2[2], rd_EM_MEM[2]);
  xor xor_10 (xor_10_out, rs2[0], rd_MEM_WB[0]);
  xor xor_11 (xor_11_out, rs2[1], rd_MEM_WB[1]);
  xor xor_12 (xor_12_out, rs2[2], rd_MEM_WB[2]);
  or or_1 (or_1_out, xor_1_out, xor_2_out, xor_3_out);
  or or_2 (or_2_out, xor_7_out, xor_8_out, xor_9_out);
  or or_3 (or_3_out, xor_10_out, xor_11_out, xor_12_out);
  not not_1 (not_1_out, or_1_out);
  or or_4 (or_4_out, xor_4_out, xor_5_out, xor_6_out);
  not not_2 (not_2_out, or_4_out);
  not not_3 (not_3_out, or_2_out);
  not not_4 (not_4_out, or_3_out);
  and and_1 (and_1_out, not_1_out, RegWrite_EX_MEM);
  and and_2 (and_2_out, not_2_out, RegWrite_MEM_WB);
  and and_3 (and_3_out, not_3_out, RegWrite_EX_MEM);
  and and_4 (and_4_out, not_4_out, RegWrite_MEM_WB);
  or or_5 (FowardA, and_1_out, and_2_out);
  or or_6 (FowardB, and_3_out, and_4_out);

  // Notes on the sheet:
  //   rs1 == rd_EX/MEM
  //   rs2 == rd_EX/MEM
  //   rs2 == rd_MEM/WB
  //   rs1 == rd_MEM/WB
endmodule
